// Logisim project mew.circ as structural Verilog: 1 circuit, main circuit main
module main (
);

  wire aBUSinc, and_2_out, buffer_2_out, clk, clock_1_out, counter_1_carry, dREGclk, init, not_1_out,
       or_1_out, pRAMin, pRAMout, register_1_q, s_r_ff_1_q, shift_register_1_p6;
  wire [7:0] bit_extender_1_out, dREGin, dREGout, pROM_data;
  wire [15:0] aBUS;

  Clock clock_1 (.out(clock_1_out));
  Register #(.width(1)) register_1 (.D(1'b1), .clk(clock_1_out), .Q(register_1_q));  // open: en, clr
  not not_1 (not_1_out, register_1_q);
  buf buffer_1 (init, not_1_out);
  S_R_Flip_Flop s_r_ff_1 (.S(init), .R(counter_1_carry), .clk(clk), .Q(s_r_ff_1_q));  // open: reset, Qn, preset
  Counter #(.max('hfeff), .width(16)) counter_1 (
    .clk(buffer_2_out), .carry(counter_1_carry), .Q(aBUS));  // open: clr, load, up, count, D
  and and_1 (clk, clock_1_out, register_1_q);
  or or_1 (or_1_out, not_1_out, shift_register_1_p6);
  // Shift_Register shift_register_1: pin names not known; wires that end beside it: clk, or_1_out, pRAMin, pRAMout, aBUSinc, shift_register_1_p6
  and and_2 (and_2_out, s_r_ff_1_q, aBUSinc);
  buf buffer_2 (buffer_2_out, and_2_out);
  Register register_2 (.D(dREGin), .clk(clk), .Q(dREGout));  // open: en, clr
  ROM #(.addrWidth(16)) pROM (.addr(aBUS), .data(pROM_data));
  // Probe on aBUS
  RAM #(.addrWidth(16), .databus("bidir")) pRAM (.addr(aBUS), .we(pRAMin), .oe(pRAMout), .clk(clk), .data(dREGout));
  LED led_1 (.in(dREGclk));
  assign bit_extender_1_out = {{7{dREGclk}}, dREGclk};  // Bit_Extender bit_extender_1
  assign dREGin = bit_extender_1_out & pROM_data;  // AND_Gate and_3, 8 bits wide

  // Other names for the same wires on the sheet: pROMout = dREGclk; sysclk = clk

  // Notes on the sheet:
  //   contents of pROM (hex, n*v repeats v):
  //   80 68 80 18 17
endmodule
